# Fritzing sketch fritzing (saved by Fritzing 0.9.3b)
breadboards: 1

parts:
  Part1 = Arduino Uno (Rev3)
  Part2 = Adafruit Mini TFT Display - 0.96in 160x80 [part_number="Adafruit 3533"]
  Part3 = Thumb Joystick
  IR1 = TSOP312.., 314.. [package=THT]

nets:
  N1: Part1.A0, Part3.HORZ
  N2: Part1.A1, Part3.VERT
  N3: Part1.D8, Part2.DC
  N4: Part1.D9_PWM, Part2.TFTRST
  N5: Part1.D10_PWM/SS, Part2.TFTCS
  N6: Part1.D11_PWM/MOSI, Part2.MOSI
  N7: Part1.D13/SCK, Part2.SCK
  GND: Part1.GND, Part2.GND, Part3.GND, IR1.GND
  N8: Part1.D7, IR1.Data
  5V: Part1.5V, Part2.VIN, Part3.VCC, IR1.Vs

notes:
  Not the same joystick, but similar enough.

custom parts:
  Adafruit Mini TFT Display - 0.96in 160x80: It's the size of your thumbnail, with glorious 160x80 pixel color... it's the Adafruit Mini TFT Breakout! This very very small display is only 0.96" diagonal, packed with RGB pixels, for making very small high-density displays. The display uses 4-wire SPI to communicate and has its own pixel-addressable frame buffer, it can be used with every kind of microcontroller. Even a very small one with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
